# Fritzing sketch TFT display  (saved by Fritzing 1.0.4)
breadboards: 1

parts:
  R2 = Resistor [tolerance=±5% power=0.25W resistance=2.2K package=THT]
  R6 = Resistor [tolerance=±5% power=0.25W resistance=5.1K package=THT]
  R7 = Resistor [tolerance=±5% power=0.25W resistance=5.1K package=THT]
  R8 = Resistor [tolerance=±5% power=0.25W resistance=5.1K package=THT]
  R9 = Resistor [tolerance=±5% power=0.25W resistance=5.1K package=THT]
  IC1 = 2.8 inch LCD SPI display with touch screen & SD card
  R10 = Resistor [tolerance=±5% power=0.25W resistance=5.1K package=THT]
  Part1 = Arduino Uno (Rev3) - ICSP
  R5 = Resistor [tolerance=±5% power=0.25W resistance=2.2K package=THT]
  R1 = Resistor [tolerance=±5% power=0.25W resistance=2.2K package=THT]
  R4 = Resistor [tolerance=±5% power=0.25W resistance=2.2K package=THT]
  R3 = Resistor [tolerance=±5% power=0.25W resistance=2.2K package=THT]

nets:
  N1: R2.Pin_0, IC1.pin6
  N2: R2.Pin_1, R6.Pin_0, Part1.D12/MISO
  N3: R6.Pin_1, R7.Pin_1, R8.Pin_1, R9.Pin_1, IC1.pin_13, R10.Pin_1, Part1.GND
  N4: R7.Pin_0, IC1.pin8, R3.Pin_1
  N5: R8.Pin_0, IC1.pin_9, R4.Pin_1
  N6: R9.Pin_0, IC1.pin_10, R1.Pin_1
  N7: IC1.pin7, IC1.pin_11, IC1.pin_14, Part1.3V3
  N8: IC1.pin_12, R10.Pin_0, R5.Pin_1
  N9: Part1.D9_PWM, R1.Pin_0
  N10: Part1.D10_PWM/SS, R5.Pin_0
  N11: Part1.D11_PWM/MOSI, R4.Pin_0
  N12: Part1.D13/SCK, R3.Pin_0

notes:
  5.1K
  2.2K
  SDO LED SCK SDI DC RESET CS GND VCC

custom parts:
  2.8 inch LCD SPI display with touch screen & SD card: A generic 2.8 inch LCD TFT 320x280 display with touchscreen and SD card slot.
